# Fritzing sketch sketch (saved by Fritzing 0.9.2b)
breadboards: 1

parts:
  Part1 = Arduino Uno (Rev3)
  RGB_LCD = Adafruit Negative RGB 2x16 LCD
  R1 = Rotary Potentiometer (Small) [maximum_resistance=100kΩ package=THT]

nets:
  N1: Part1.D8, RGB_LCD.no_name_yet#105, RGB_LCD.no_name_yet#106
  N2: Part1.D9_PWM, RGB_LCD.no_name_yet#109, RGB_LCD.no_name_yet#110
  N3: Part1.D10_PWM/SS, RGB_LCD.no_name_yet#111
  N4: Part1.D11_PWM/MOSI, RGB_LCD.no_name_yet#112
  N5: Part1.D12/MISO, Part1.5V, RGB_LCD.no_name_yet#101, RGB_LCD.no_name_yet#113, RGB_LCD.no_name_yet#114, R1.leg2
  N6: Part1.D3_PWM, RGB_LCD.no_name_yet#115
  N7: Part1.D5_PWM, RGB_LCD.no_name_yet#116
  N8: Part1.D6_PWM, RGB_LCD.no_name_yet#117
  N9: Part1.D7, RGB_LCD.no_name_yet#103
  N10: Part1.GND, RGB_LCD.no_name_yet#100, RGB_LCD.no_name_yet#104, R1.leg1
  N11: RGB_LCD.no_name_yet#102, R1.wiper

custom parts:
  Adafruit Negative RGB 2x16 LCD: Adafruit Negative 2x16 LCD Display with RGB Backlight
